// Logisim project project_demo.circ as structural Verilog: 9 circuits, main circuit main
module main (
  input  [15:0] bus_0
);

  wire cdm_16_1_p1, cdm_16_1_p2, cdm_16_1_p4, cdm_16_1_p5, cdm_16_1_p6, cdm_16_1_p7, cdm_16_1_p8,
       cdm_16_1_p9, chip_1_out_13, chip_2_out_13, chip_3_out_13, chip_5_out_13, chip_6_out_13, chip_7_out_13,
       chip_8_out_13, chip_9_out_13, chip_10_out_13, chip_11_out_13, chip_12_out_13, chip_13_out_13,
       chip_14_out_13, chip_15_out_13, chip_16_out_13, chip_17_out_13, chip_18_out_13, chip_19_out_13,
       chip_20_out_13, chip_21_out_13, chip_22_out_13, chip_23_out_13, chip_24_out_13, chip_25_out_13,
       chip_26_out_13, chip_27_out_13, chip_28_out_13, chip_29_out_13, chip_30_out_13, chip_31_out_13,
       chip_32_out_13, clock, clock_2_out, comparator_4_gt, comparator_5_lt, comparator_6_eq,
       comparator_7_gt, comparator_8_lt, mem, not_1_out, or_1_out, pull_resistor_1_node,
       pull_resistor_3_node, pull_resistor_5_node, rd, use_mmio, word;
  wire [3:0] scoreboard_1_out_2, scoreboard_1_out_3, scoreboard_1_out_4, scoreboard_1_out_5,
       scoreboard_1_out_6, stick_x, stick_y, subtractor_5_out;
  wire [4:0] chip_1_out_7, chip_2_out_7, chip_3_out_7, chip_4_out_7, chip_5_out_7, chip_6_out_7,
       chip_7_out_7, chip_8_out_7, chip_9_out_7, chip_10_out_7, chip_11_out_7, chip_12_out_7, chip_13_out_7,
       chip_14_out_7, chip_15_out_7, chip_16_out_7, chip_17_out_7, chip_18_out_7, chip_19_out_7,
       chip_20_out_7, chip_21_out_7, chip_22_out_7, chip_23_out_7, chip_24_out_7, chip_25_out_7,
       chip_26_out_7, chip_27_out_7, chip_28_out_7, chip_29_out_7, chip_30_out_7, chip_31_out_7;
  wire [5:5] comparator_1_lt, comparator_2_lt, comparator_3_lt;
  wire [6:0] adder_1_out;
  wire [10:0] chip_1_sprite1_2, chip_1_sprite2_2, chip_1_sprite3_2, chip_2_sprite1_2, chip_2_sprite2_2,
       chip_2_sprite3_2, chip_3_sprite1_2, chip_3_sprite2_2, chip_3_sprite3_2, chip_4_sprite1_2,
       chip_4_sprite2_2, chip_4_sprite3_2, chip_5_sprite1_2, chip_5_sprite2_2, chip_5_sprite3_2,
       chip_6_sprite1_2, chip_6_sprite2_2, chip_6_sprite3_2, chip_7_sprite1_2, chip_7_sprite2_2,
       chip_7_sprite3_2, chip_8_sprite1_2, chip_8_sprite2_2, chip_8_sprite3_2, chip_9_sprite1_2,
       chip_9_sprite2_2, chip_9_sprite3_2, chip_10_sprite1_2, chip_10_sprite2_2, chip_10_sprite3_2,
       chip_11_sprite1_2, chip_11_sprite2_2, chip_11_sprite3_2, chip_12_sprite1_2, chip_12_sprite2_2,
       chip_12_sprite3_2, chip_13_sprite1_2, chip_13_sprite2_2, chip_13_sprite3_2, chip_14_sprite1_2,
       chip_14_sprite2_2, chip_14_sprite3_2, chip_15_sprite1_2, chip_15_sprite2_2, chip_15_sprite3_2,
       chip_16_sprite1_2, chip_16_sprite2_2, chip_16_sprite3_2, chip_17_sprite1_2, chip_17_sprite2_2,
       chip_17_sprite3_2, chip_18_sprite1_2, chip_18_sprite2_2, chip_18_sprite3_2, chip_19_sprite1_2,
       chip_19_sprite2_2, chip_19_sprite3_2, chip_20_sprite1_2, chip_20_sprite2_2, chip_20_sprite3_2,
       chip_21_sprite1_2, chip_21_sprite2_2, chip_21_sprite3_2, chip_22_sprite1_2, chip_22_sprite2_2,
       chip_22_sprite3_2, chip_23_sprite1_2, chip_23_sprite2_2, chip_23_sprite3_2, chip_24_sprite1_2,
       chip_24_sprite2_2, chip_24_sprite3_2, chip_25_sprite1_2, chip_25_sprite2_2, chip_25_sprite3_2,
       chip_26_sprite1_2, chip_26_sprite2_2, chip_26_sprite3_2, chip_27_sprite1_2, chip_27_sprite2_2,
       chip_27_sprite3_2, chip_28_sprite1_2, chip_28_sprite2_2, chip_28_sprite3_2, chip_29_sprite1_2,
       chip_29_sprite2_2, chip_29_sprite3_2, chip_30_sprite1_2, chip_30_sprite2_2, chip_30_sprite3_2,
       chip_31_sprite1_2, chip_31_sprite2_2, chip_31_sprite3_2;
  wire [15:0] _1t1_x, _1t1_y, _2t1_x, _2t1_y, _12, addr, cdm_16_1_p15, chip_1_out_12, chip_2_out_12,
       chip_3_out_12, chip_5_out_12, chip_6_out_12, chip_7_out_12, chip_8_out_12, chip_9_out_12,
       chip_10_out_12, chip_11_out_12, chip_12_out_12, chip_13_out_12, chip_14_out_12, chip_15_out_12,
       chip_16_out_12, chip_17_out_12, chip_18_out_12, chip_19_out_12, chip_20_out_12, chip_21_out_12,
       chip_22_out_12, chip_23_out_12, chip_24_out_12, chip_25_out_12, chip_26_out_12, chip_27_out_12,
       chip_28_out_12, chip_29_out_12, chip_30_out_12, chip_31_out_12, chip_32_out_12, column,
       controlled_buffer_1_out, counter, data, distribute_regs_1_bus_0_7, distribute_regs_1_bus_0_8,
       distribute_regs_1_bus_0_9, distribute_regs_1_bus_0_10, distribute_regs_1_bus_0_11,
       distribute_regs_1_bus_0_12, distribute_regs_1_bus_0_14, mario_x, mario_y, multiplexer_1_out,
       multiplexer_2_out, out, pull_resistor_2_node, pull_resistor_4_node, shifter_1_out, signal,
       subtractor_1_out, subtractor_2_out, subtractor_3_out;
  wire [15:7] adder_1_out_2;
  wire [31:0] chip_1_out_9, chip_2_out_9, chip_3_out_9, chip_4_out_9, chip_5_out_9, chip_6_out_9,
       chip_7_out_9, chip_8_out_9, chip_9_out_9, chip_10_out_9, chip_11_out_9, chip_12_out_9, chip_13_out_9,
       chip_14_out_9, chip_15_out_9, chip_16_out_9, chip_17_out_9, chip_18_out_9, chip_19_out_9,
       chip_20_out_9, chip_21_out_9, chip_22_out_9, chip_23_out_9, chip_24_out_9, chip_25_out_9,
       chip_26_out_9, chip_27_out_9, chip_28_out_9, chip_29_out_9, chip_30_out_9, chip_31_out_9,
       chip_32_out_9;

  // Probe on bus_0
  Comparator #(.width(16)) comparator_1 (.a(mario_x), .b(16'h1d), .lt(comparator_1_lt[5]));  // open: gt, eq
  Comparator #(.width(16)) comparator_2 (.a(_1t1_x), .b(16'h1d), .lt(comparator_2_lt[5]));  // open: gt, eq
  // Probe on cdm_16_1_p5
  // Probe on cdm_16_1_p6
  // Probe on cdm_16_1_p4
  // Probe on cdm_16_1_p2
  // CdM_16 cdm_16_1: pin names not known; wires that end beside it: cdm_16_1_p1, cdm_16_1_p2, clock, cdm_16_1_p4, cdm_16_1_p5, cdm_16_1_p6, cdm_16_1_p7, cdm_16_1_p8, cdm_16_1_p9, mem, rd, word, addr, out, cdm_16_1_p15
  // Probe on cdm_16_1_p1
  Clock clock_1 (.out(clock));
  Comparator #(.width(16)) comparator_3 (.a(_2t1_x), .b(16'h1d), .lt(comparator_3_lt[5]));  // open: gt, eq
  // Probe on cdm_16_1_p8
  // Probe on cdm_16_1_p7
  Hex_Digit_Display hex_digit_display_1 (.value(scoreboard_1_out_2));  // open: dp
  // Probe on counter[13:0]
  Subtractor #(.width(16)) subtractor_1 (.a(16'h1d), .b(mario_y), .out(subtractor_1_out));  // open: bin, bout
  Subtractor #(.width(16)) subtractor_2 (.a(16'h1d), .b(_2t1_y), .out(subtractor_2_out));  // open: bin, bout
  // Probe on cdm_16_1_p9
  assign controlled_buffer_1_out = rd ? data : 16'bz;  // Controlled_Buffer controlled_buffer_1
  joystick joystick_1 (
    .bus_0(cdm_16_1_p15), .input_1(stick_x), .input_2(stick_y), .addr(addr), .data(controlled_buffer_1_out),
    .mem(mem), .rd(rd));
  Hex_Digit_Display hex_digit_display_2 (.value(scoreboard_1_out_6));  // open: dp
  Hex_Digit_Display hex_digit_display_3 (.value(scoreboard_1_out_4));  // open: dp
  scoreboard scoreboard_1 (
    .in_1(counter[13:0]), .out_3(scoreboard_1_out_3), .out_4(scoreboard_1_out_4), .out_5(scoreboard_1_out_5),
    .out_6(scoreboard_1_out_6), .out_2(scoreboard_1_out_2));
  Subtractor #(.width(16)) subtractor_3 (.a(16'h1d), .b(_1t1_y), .out(subtractor_3_out));  // open: bin, bout
  // Probe on addr
  Subtractor #(.width(16)) subtractor_4 (.a(distribute_regs_1_bus_0_14), .b(16'h1), .out(column));  // open: bin, bout
  not not_1 (not_1_out, rd);
  assign data = not_1_out ? out : 16'bz;  // Controlled_Buffer controlled_buffer_2
  Hex_Digit_Display hex_digit_display_4 (.value(scoreboard_1_out_3));  // open: dp
  Hex_Digit_Display hex_digit_display_5 (.value(scoreboard_1_out_5));  // open: dp
  // Probe on distribute_regs_1_bus_0_12
  // Probe on distribute_regs_1_bus_0_11
  // Debugger debugger_1: pin names not known; wires that end beside it: use_mmio
  Pull_Resistor pull_resistor_1 (.node(pull_resistor_1_node));
  Pull_Resistor pull_resistor_2 (.node(pull_resistor_2_node));
  Pull_Resistor pull_resistor_3 (.node(pull_resistor_3_node));
  Pull_Resistor pull_resistor_4 (.node(pull_resistor_4_node));
  Pull_Resistor #(.pull(1)) pull_resistor_5 (.node(pull_resistor_5_node));
  assign pull_resistor_4_node = use_mmio ? addr : 16'bz;  // Controlled_Buffer controlled_buffer_3
  assign pull_resistor_2_node = use_mmio ? out : 16'bz;  // Controlled_Buffer controlled_buffer_4
  assign pull_resistor_1_node = use_mmio ? mem : 1'bz;  // Controlled_Buffer controlled_buffer_5
  assign pull_resistor_5_node = use_mmio ? rd : 1'bz;  // Controlled_Buffer controlled_buffer_6
  assign pull_resistor_3_node = use_mmio ? clock : 1'bz;  // Controlled_Buffer controlled_buffer_7
  DotMatrix #(.matrixcols(32), .matrixrows(32)) dotmatrix_1 (
    .col0(chip_4_out_9), .col1(chip_2_out_9), .col2(chip_5_out_9), .col3(chip_3_out_9), .col4(chip_1_out_9),
    .col5(chip_9_out_9), .col6(chip_7_out_9), .col7(chip_8_out_9), .col8(chip_11_out_9),
    .col9(chip_12_out_9), .col10(chip_13_out_9), .col11(chip_10_out_9), .col12(chip_6_out_9),
    .col13(chip_17_out_9), .col14(chip_19_out_9), .col15(chip_18_out_9), .col16(chip_20_out_9),
    .col17(chip_14_out_9), .col18(chip_15_out_9), .col19(chip_16_out_9), .col20(chip_21_out_9),
    .col21(chip_25_out_9), .col22(chip_23_out_9), .col23(chip_29_out_9), .col24(chip_24_out_9),
    .col25(chip_27_out_9), .col26(chip_28_out_9), .col27(chip_22_out_9), .col28(chip_26_out_9),
    .col29(chip_30_out_9), .col30(chip_31_out_9), .col31(chip_32_out_9));
  chip chip_1 (
    .in_1(chip_3_out_7), .sprite1(chip_3_sprite1_2), .sprite2(chip_3_sprite2_2), .out_7(chip_1_out_7),
    .out_9(chip_1_out_9), .sprite1_2(chip_1_sprite1_2), .sprite2_2(chip_1_sprite2_2), .in_6(chip_9_out_13),
    .out_12(chip_1_out_12), .in_5(chip_9_out_12), .out_13(chip_1_out_13), .sprite3_2(chip_1_sprite3_2),
    .sprite3(chip_3_sprite3_2));
  chip chip_2 (
    .in_1(chip_4_out_7), .sprite1(chip_4_sprite1_2), .sprite2(chip_4_sprite2_2), .out_7(chip_2_out_7),
    .out_9(chip_2_out_9), .sprite1_2(chip_2_sprite1_2), .sprite2_2(chip_2_sprite2_2), .in_6(chip_5_out_13),
    .out_12(chip_2_out_12), .in_5(chip_5_out_12), .out_13(chip_2_out_13), .sprite3_2(chip_2_sprite3_2),
    .sprite3(chip_4_sprite3_2));
  chip chip_3 (
    .in_1(chip_5_out_7), .sprite1(chip_5_sprite1_2), .sprite2(chip_5_sprite2_2), .out_7(chip_3_out_7),
    .out_9(chip_3_out_9), .sprite1_2(chip_3_sprite1_2), .sprite2_2(chip_3_sprite2_2), .in_6(chip_1_out_13),
    .out_12(chip_3_out_12), .in_5(chip_1_out_12), .out_13(chip_3_out_13), .sprite3_2(chip_3_sprite3_2),
    .sprite3(chip_5_sprite3_2));
  chip chip_4 (
    .in_1({5{1'b0}}), .sprite1({subtractor_1_out[4:0], comparator_1_lt[5], mario_x[4:0]}),
    .sprite2({subtractor_2_out[4:0], comparator_3_lt[5], _2t1_x[4:0]}), .out_7(chip_4_out_7),
    .out_9(chip_4_out_9), .sprite1_2(chip_4_sprite1_2), .sprite2_2(chip_4_sprite2_2), .in_6(chip_2_out_13),
    .in_5(chip_2_out_12), .sprite3_2(chip_4_sprite3_2),
    .sprite3({subtractor_3_out[4:0], comparator_2_lt[5], _1t1_x[4:0]}));  // open: out_12, out_13
  chip chip_5 (
    .in_1(chip_2_out_7), .sprite1(chip_2_sprite1_2), .sprite2(chip_2_sprite2_2), .out_7(chip_5_out_7),
    .out_9(chip_5_out_9), .sprite1_2(chip_5_sprite1_2), .sprite2_2(chip_5_sprite2_2), .in_6(chip_3_out_13),
    .out_12(chip_5_out_12), .in_5(chip_3_out_12), .out_13(chip_5_out_13), .sprite3_2(chip_5_sprite3_2),
    .sprite3(chip_2_sprite3_2));
  // Probe on mario_x
  distribute_regs distribute_regs_1 (
    .addr(pull_resistor_4_node), .out(pull_resistor_2_node), .bus_0(mario_x), .clock(pull_resistor_3_node),
    .bus_0_2(mario_y), .bus_0_3(_1t1_x), .bus_0_4(_1t1_y), .bus_0_5(_2t1_x), .bus_0_6(_2t1_y),
    .bus_0_7(distribute_regs_1_bus_0_7), .mem(pull_resistor_1_node), .bus_0_8(distribute_regs_1_bus_0_8),
    .bus_0_9(distribute_regs_1_bus_0_9), .bus_0_10(distribute_regs_1_bus_0_10),
    .bus_0_11(distribute_regs_1_bus_0_11), .bus_0_12(distribute_regs_1_bus_0_12), .bus_0_13(signal),
    .bus_0_14(distribute_regs_1_bus_0_14), .bus_0_15(_12), .bus_0_16(counter), .rd(pull_resistor_5_node));
  // Probe on distribute_regs_1_bus_0_8
  // Probe on distribute_regs_1_bus_0_9
  // Probe on distribute_regs_1_bus_0_10
  chip chip_6 (
    .in_1(chip_10_out_7), .sprite1(chip_10_sprite1_2), .sprite2(chip_10_sprite2_2), .out_7(chip_6_out_7),
    .out_9(chip_6_out_9), .sprite1_2(chip_6_sprite1_2), .sprite2_2(chip_6_sprite2_2), .in_6(chip_17_out_13),
    .out_12(chip_6_out_12), .in_5(chip_17_out_12), .out_13(chip_6_out_13), .sprite3_2(chip_6_sprite3_2),
    .sprite3(chip_10_sprite3_2));
  chip chip_7 (
    .in_1(chip_9_out_7), .sprite1(chip_9_sprite1_2), .sprite2(chip_9_sprite2_2), .out_7(chip_7_out_7),
    .out_9(chip_7_out_9), .sprite1_2(chip_7_sprite1_2), .sprite2_2(chip_7_sprite2_2), .in_6(chip_8_out_13),
    .out_12(chip_7_out_12), .in_5(chip_8_out_12), .out_13(chip_7_out_13), .sprite3_2(chip_7_sprite3_2),
    .sprite3(chip_9_sprite3_2));
  chip chip_8 (
    .in_1(chip_7_out_7), .sprite1(chip_7_sprite1_2), .sprite2(chip_7_sprite2_2), .out_7(chip_8_out_7),
    .out_9(chip_8_out_9), .sprite1_2(chip_8_sprite1_2), .sprite2_2(chip_8_sprite2_2), .in_6(chip_11_out_13),
    .out_12(chip_8_out_12), .in_5(chip_11_out_12), .out_13(chip_8_out_13), .sprite3_2(chip_8_sprite3_2),
    .sprite3(chip_7_sprite3_2));
  chip chip_9 (
    .in_1(chip_1_out_7), .sprite1(chip_1_sprite1_2), .sprite2(chip_1_sprite2_2), .out_7(chip_9_out_7),
    .out_9(chip_9_out_9), .sprite1_2(chip_9_sprite1_2), .sprite2_2(chip_9_sprite2_2), .in_6(chip_7_out_13),
    .out_12(chip_9_out_12), .in_5(chip_7_out_12), .out_13(chip_9_out_13), .sprite3_2(chip_9_sprite3_2),
    .sprite3(chip_1_sprite3_2));
  chip chip_10 (
    .in_1(chip_13_out_7), .sprite1(chip_13_sprite1_2), .sprite2(chip_13_sprite2_2), .out_7(chip_10_out_7),
    .out_9(chip_10_out_9), .sprite1_2(chip_10_sprite1_2), .sprite2_2(chip_10_sprite2_2),
    .in_6(chip_6_out_13), .out_12(chip_10_out_12), .in_5(chip_6_out_12), .out_13(chip_10_out_13),
    .sprite3_2(chip_10_sprite3_2), .sprite3(chip_13_sprite3_2));
  chip chip_11 (
    .in_1(chip_8_out_7), .sprite1(chip_8_sprite1_2), .sprite2(chip_8_sprite2_2), .out_7(chip_11_out_7),
    .out_9(chip_11_out_9), .sprite1_2(chip_11_sprite1_2), .sprite2_2(chip_11_sprite2_2),
    .in_6(chip_12_out_13), .out_12(chip_11_out_12), .in_5(chip_12_out_12), .out_13(chip_11_out_13),
    .sprite3_2(chip_11_sprite3_2), .sprite3(chip_8_sprite3_2));
  chip chip_12 (
    .in_1(chip_11_out_7), .sprite1(chip_11_sprite1_2), .sprite2(chip_11_sprite2_2), .out_7(chip_12_out_7),
    .out_9(chip_12_out_9), .sprite1_2(chip_12_sprite1_2), .sprite2_2(chip_12_sprite2_2),
    .in_6(chip_13_out_13), .out_12(chip_12_out_12), .in_5(chip_13_out_12), .out_13(chip_12_out_13),
    .sprite3_2(chip_12_sprite3_2), .sprite3(chip_11_sprite3_2));
  chip chip_13 (
    .in_1(chip_12_out_7), .sprite1(chip_12_sprite1_2), .sprite2(chip_12_sprite2_2), .out_7(chip_13_out_7),
    .out_9(chip_13_out_9), .sprite1_2(chip_13_sprite1_2), .sprite2_2(chip_13_sprite2_2),
    .in_6(chip_10_out_13), .out_12(chip_13_out_12), .in_5(chip_10_out_12), .out_13(chip_13_out_13),
    .sprite3_2(chip_13_sprite3_2), .sprite3(chip_12_sprite3_2));
  // Probe on distribute_regs_1_bus_0_7
  chip chip_14 (
    .in_1(chip_20_out_7), .sprite1(chip_20_sprite1_2), .sprite2(chip_20_sprite2_2), .out_7(chip_14_out_7),
    .out_9(chip_14_out_9), .sprite1_2(chip_14_sprite1_2), .sprite2_2(chip_14_sprite2_2),
    .in_6(chip_15_out_13), .out_12(chip_14_out_12), .in_5(chip_15_out_12), .out_13(chip_14_out_13),
    .sprite3_2(chip_14_sprite3_2), .sprite3(chip_20_sprite3_2));
  chip chip_15 (
    .in_1(chip_14_out_7), .sprite1(chip_14_sprite1_2), .sprite2(chip_14_sprite2_2), .out_7(chip_15_out_7),
    .out_9(chip_15_out_9), .sprite1_2(chip_15_sprite1_2), .sprite2_2(chip_15_sprite2_2),
    .in_6(chip_16_out_13), .out_12(chip_15_out_12), .in_5(chip_16_out_12), .out_13(chip_15_out_13),
    .sprite3_2(chip_15_sprite3_2), .sprite3(chip_14_sprite3_2));
  chip chip_16 (
    .in_1(chip_15_out_7), .sprite1(chip_15_sprite1_2), .sprite2(chip_15_sprite2_2), .out_7(chip_16_out_7),
    .out_9(chip_16_out_9), .sprite1_2(chip_16_sprite1_2), .sprite2_2(chip_16_sprite2_2),
    .in_6(chip_21_out_13), .out_12(chip_16_out_12), .in_5(chip_21_out_12), .out_13(chip_16_out_13),
    .sprite3_2(chip_16_sprite3_2), .sprite3(chip_15_sprite3_2));
  chip chip_17 (
    .in_1(chip_6_out_7), .sprite1(chip_6_sprite1_2), .sprite2(chip_6_sprite2_2), .out_7(chip_17_out_7),
    .out_9(chip_17_out_9), .sprite1_2(chip_17_sprite1_2), .sprite2_2(chip_17_sprite2_2),
    .in_6(chip_19_out_13), .out_12(chip_17_out_12), .in_5(chip_19_out_12), .out_13(chip_17_out_13),
    .sprite3_2(chip_17_sprite3_2), .sprite3(chip_6_sprite3_2));
  chip chip_18 (
    .in_1(chip_19_out_7), .sprite1(chip_19_sprite1_2), .sprite2(chip_19_sprite2_2), .out_7(chip_18_out_7),
    .out_9(chip_18_out_9), .sprite1_2(chip_18_sprite1_2), .sprite2_2(chip_18_sprite2_2),
    .in_6(chip_20_out_13), .out_12(chip_18_out_12), .in_5(chip_20_out_12), .out_13(chip_18_out_13),
    .sprite3_2(chip_18_sprite3_2), .sprite3(chip_19_sprite3_2));
  chip chip_19 (
    .in_1(chip_17_out_7), .sprite1(chip_17_sprite1_2), .sprite2(chip_17_sprite2_2), .out_7(chip_19_out_7),
    .out_9(chip_19_out_9), .sprite1_2(chip_19_sprite1_2), .sprite2_2(chip_19_sprite2_2),
    .in_6(chip_18_out_13), .out_12(chip_19_out_12), .in_5(chip_18_out_12), .out_13(chip_19_out_13),
    .sprite3_2(chip_19_sprite3_2), .sprite3(chip_17_sprite3_2));
  chip chip_20 (
    .in_1(chip_18_out_7), .sprite1(chip_18_sprite1_2), .sprite2(chip_18_sprite2_2), .out_7(chip_20_out_7),
    .out_9(chip_20_out_9), .sprite1_2(chip_20_sprite1_2), .sprite2_2(chip_20_sprite2_2),
    .in_6(chip_14_out_13), .out_12(chip_20_out_12), .in_5(chip_14_out_12), .out_13(chip_20_out_13),
    .sprite3_2(chip_20_sprite3_2), .sprite3(chip_18_sprite3_2));
  chip chip_21 (
    .in_1(chip_16_out_7), .sprite1(chip_16_sprite1_2), .sprite2(chip_16_sprite2_2), .out_7(chip_21_out_7),
    .out_9(chip_21_out_9), .sprite1_2(chip_21_sprite1_2), .sprite2_2(chip_21_sprite2_2),
    .in_6(chip_25_out_13), .out_12(chip_21_out_12), .in_5(chip_25_out_12), .out_13(chip_21_out_13),
    .sprite3_2(chip_21_sprite3_2), .sprite3(chip_16_sprite3_2));
  // Probe on mario_x
  // Probe on mario_y
  // Probe on _1t1_x
  // Probe on _1t1_y
  // Probe on _2t1_x
  // Probe on _2t1_y
  // Probe on counter
  // Probe on column
  // Probe on signal
  chip chip_22 (
    .in_1(chip_28_out_7), .sprite1(chip_28_sprite1_2), .sprite2(chip_28_sprite2_2), .out_7(chip_22_out_7),
    .out_9(chip_22_out_9), .sprite1_2(chip_22_sprite1_2), .sprite2_2(chip_22_sprite2_2),
    .in_6(chip_26_out_13), .out_12(chip_22_out_12), .in_5(chip_26_out_12), .out_13(chip_22_out_13),
    .sprite3_2(chip_22_sprite3_2), .sprite3(chip_28_sprite3_2));
  chip chip_23 (
    .in_1(chip_25_out_7), .sprite1(chip_25_sprite1_2), .sprite2(chip_25_sprite2_2), .out_7(chip_23_out_7),
    .out_9(chip_23_out_9), .sprite1_2(chip_23_sprite1_2), .sprite2_2(chip_23_sprite2_2),
    .in_6(chip_29_out_13), .out_12(chip_23_out_12), .in_5(chip_29_out_12), .out_13(chip_23_out_13),
    .sprite3_2(chip_23_sprite3_2), .sprite3(chip_25_sprite3_2));
  chip chip_24 (
    .in_1(chip_29_out_7), .sprite1(chip_29_sprite1_2), .sprite2(chip_29_sprite2_2), .out_7(chip_24_out_7),
    .out_9(chip_24_out_9), .sprite1_2(chip_24_sprite1_2), .sprite2_2(chip_24_sprite2_2),
    .in_6(chip_27_out_13), .out_12(chip_24_out_12), .in_5(chip_27_out_12), .out_13(chip_24_out_13),
    .sprite3_2(chip_24_sprite3_2), .sprite3(chip_29_sprite3_2));
  chip chip_25 (
    .in_1(chip_21_out_7), .sprite1(chip_21_sprite1_2), .sprite2(chip_21_sprite2_2), .out_7(chip_25_out_7),
    .out_9(chip_25_out_9), .sprite1_2(chip_25_sprite1_2), .sprite2_2(chip_25_sprite2_2),
    .in_6(chip_23_out_13), .out_12(chip_25_out_12), .in_5(chip_23_out_12), .out_13(chip_25_out_13),
    .sprite3_2(chip_25_sprite3_2), .sprite3(chip_21_sprite3_2));
  chip chip_26 (
    .in_1(chip_22_out_7), .sprite1(chip_22_sprite1_2), .sprite2(chip_22_sprite2_2), .out_7(chip_26_out_7),
    .out_9(chip_26_out_9), .sprite1_2(chip_26_sprite1_2), .sprite2_2(chip_26_sprite2_2),
    .in_6(chip_30_out_13), .out_12(chip_26_out_12), .in_5(chip_30_out_12), .out_13(chip_26_out_13),
    .sprite3_2(chip_26_sprite3_2), .sprite3(chip_22_sprite3_2));
  chip chip_27 (
    .in_1(chip_24_out_7), .sprite1(chip_24_sprite1_2), .sprite2(chip_24_sprite2_2), .out_7(chip_27_out_7),
    .out_9(chip_27_out_9), .sprite1_2(chip_27_sprite1_2), .sprite2_2(chip_27_sprite2_2),
    .in_6(chip_28_out_13), .out_12(chip_27_out_12), .in_5(chip_28_out_12), .out_13(chip_27_out_13),
    .sprite3_2(chip_27_sprite3_2), .sprite3(chip_24_sprite3_2));
  chip chip_28 (
    .in_1(chip_27_out_7), .sprite1(chip_27_sprite1_2), .sprite2(chip_27_sprite2_2), .out_7(chip_28_out_7),
    .out_9(chip_28_out_9), .sprite1_2(chip_28_sprite1_2), .sprite2_2(chip_28_sprite2_2),
    .in_6(chip_22_out_13), .out_12(chip_28_out_12), .in_5(chip_22_out_12), .out_13(chip_28_out_13),
    .sprite3_2(chip_28_sprite3_2), .sprite3(chip_27_sprite3_2));
  chip chip_29 (
    .in_1(chip_23_out_7), .sprite1(chip_23_sprite1_2), .sprite2(chip_23_sprite2_2), .out_7(chip_29_out_7),
    .out_9(chip_29_out_9), .sprite1_2(chip_29_sprite1_2), .sprite2_2(chip_29_sprite2_2),
    .in_6(chip_24_out_13), .out_12(chip_29_out_12), .in_5(chip_24_out_12), .out_13(chip_29_out_13),
    .sprite3_2(chip_29_sprite3_2), .sprite3(chip_23_sprite3_2));
  Comparator #(.width(16)) comparator_4 (.a(addr), .b(16'hfeff), .gt(comparator_4_gt));  // open: eq, lt
  Comparator #(.width(16)) comparator_5 (.a(addr), .b(16'hff11), .lt(comparator_5_lt));  // open: gt, eq
  chip chip_30 (
    .in_1(chip_26_out_7), .sprite1(chip_26_sprite1_2), .sprite2(chip_26_sprite2_2), .out_7(chip_30_out_7),
    .out_9(chip_30_out_9), .sprite1_2(chip_30_sprite1_2), .sprite2_2(chip_30_sprite2_2),
    .in_6(chip_31_out_13), .out_12(chip_30_out_12), .in_5(chip_31_out_12), .out_13(chip_30_out_13),
    .sprite3_2(chip_30_sprite3_2), .sprite3(chip_26_sprite3_2));
  chip chip_31 (
    .in_1(chip_30_out_7), .sprite1(chip_30_sprite1_2), .sprite2(chip_30_sprite2_2), .out_7(chip_31_out_7),
    .out_9(chip_31_out_9), .sprite1_2(chip_31_sprite1_2), .sprite2_2(chip_31_sprite2_2),
    .in_6(chip_32_out_13), .out_12(chip_31_out_12), .in_5(chip_32_out_12), .out_13(chip_31_out_13),
    .sprite3_2(chip_31_sprite3_2), .sprite3(chip_30_sprite3_2));
  chip chip_32 (
    .in_1(chip_31_out_7), .sprite1(chip_31_sprite1_2), .sprite2(chip_31_sprite2_2), .out_9(chip_32_out_9),
    .in_6(signal[1]), .out_12(chip_32_out_12), .in_5(multiplexer_1_out), .out_13(chip_32_out_13),
    .sprite3(chip_31_sprite3_2));  // open: out_7, sprite1_2, sprite2_2, sprite3_2
  Clock clock_2 (.out(clock_2_out));
  and and_1 (use_mmio, comparator_4_gt, comparator_5_lt, mem, ~rd);  // AND_Gate
  Joystick joystick_2 (.x(stick_x), .y(stick_y));
  // RAM ram_1: pin names not known; wires that end beside it: stick_x, stick_y, addr, word, mem, clock_2_out, rd, data
  // Probe on stick_x
  // Probe on stick_y
  Subtractor #(.width(4)) subtractor_5 (.a(column[3:0]), .b(4'b0001), .out(subtractor_5_out));  // open: bin, bout
  // Probe on subtractor_5_out
  Multiplexer #(.width(16), .enable("false")) multiplexer_1 (
    .in0(multiplexer_2_out), .in1({16{1'b0}}), .out(multiplexer_1_out), .sel(comparator_6_eq));
  Shifter #(.width(16)) shifter_1 (.in(16'h1), .\dist (subtractor_5_out), .out(shifter_1_out));
  Multiplexer #(.width(16), .enable("false")) multiplexer_2 (
    .in0(shifter_1_out), .in1({{9{1'b0}}, adder_1_out}), .out(multiplexer_2_out), .sel(or_1_out));
  Comparator #(.width(4)) comparator_6 (.a(column[3:0]), .b(4'b0000), .eq(comparator_6_eq));  // open: gt, lt
  // Probe on {{9{1'b0}}, adder_1_out}
  Comparator #(.width(16)) comparator_7 (.a(column), .b(16'h10), .gt(comparator_7_gt));  // open: eq, lt
  Comparator #(.width(16), .mode("unsigned")) comparator_8 (
    .a(column), .b({16{1'b0}}), .lt(comparator_8_lt));  // open: gt, eq
  // Probe on {{9{1'b0}}, adder_1_out}
  or or_1 (or_1_out, comparator_7_gt, comparator_8_lt);
  Adder #(.width(16)) adder_1 (.a(16'h1), .b(column), .out({adder_1_out_2, adder_1_out}));  // open: cin, cout
endmodule

module scoreboard (
  input  [13:0] in_1,
  output [3:0] out_2,
  output [3:0] out_3,
  output [3:0] out_4,
  output [3:0] out_5,
  output [3:0] out_6
);

  wire [4:1] divider_4_out;
  wire [4:4] divider_4_rem;
  wire [7:0] divider_3_out;
  wire [7:4] divider_3_rem;
  wire [10:0] divider_2_out;
  wire [10:4] divider_2_rem;
  wire [13:0] divider_1_out;
  wire [13:4] divider_1_rem;

  // Probe on 14'ha
  // Probe on in_1
  Divider #(.width(14)) divider_1 (
    .a(in_1), .b(14'ha), .out(divider_1_out), .rem({divider_1_rem, out_5}));  // open: upper
  // Probe on out_5
  // Probe on divider_1_out[10:0]
  Divider #(.width(11)) divider_2 (
    .a(divider_1_out[10:0]), .b(11'ha), .out(divider_2_out), .rem({divider_2_rem, out_3}));  // open: upper
  // Probe on out_3
  // Probe on divider_2_out[7:0]
  // Probe on divider_3_out[4:0]
  Divider divider_3 (
    .a(divider_2_out[7:0]), .b(8'ha), .out(divider_3_out), .rem({divider_3_rem, out_4}));  // open: upper
  // Probe on out_4
  // Probe on out_2[0]
  Divider #(.width(5)) divider_4 (
    .a(divider_3_out[4:0]), .b(5'b01010), .out({divider_4_out, out_2[0]}), .rem({divider_4_rem[4], out_6}));  // open: upper

  assign out_2[3:1] = 3'b000;
endmodule

module chip (
  input  [4:0] in_1,
  input  [10:0] sprite1,
  input  [10:0] sprite2,
  input  [10:0] sprite3,
  input  [15:0] in_5,
  input  in_6,
  output [4:0] out_7,
  output [10:0] sprite1_2,
  output [31:0] out_9,
  output [10:0] sprite2_2,
  output [10:0] sprite3_2,
  output [15:0] out_12,
  output out_13
);

  wire and_1_out, and_2_out, and_3_out, comparator_1_lt, comparator_2_eq, comparator_2_gt, comparator_3_lt,
       comparator_4_eq, comparator_4_gt, comparator_5_lt, comparator_6_eq, comparator_6_gt, or_1_out,
       or_2_out, or_3_out;
  wire [4:0] subtractor_1_out, subtractor_2_out, subtractor_3_out;
  wire [31:0] shifter_1_out, shifter_2_out, shifter_3_out, super_mux2_1_out_3, super_mux3_1_out_3,
       super_mux_1_out_3;

  Adder #(.width(5)) adder_1 (.a(in_1), .b(5'b00001), .out(out_7));  // open: cin, cout
  // Probe on sprite1[4:0]
  // Probe on sprite1[10:6]
  // Probe on sprite2[4:0]
  // Probe on sprite2[10:6]
  // Probe on sprite3[4:0]
  // Probe on sprite3[10:6]
  Subtractor #(.width(5)) subtractor_1 (.a(out_7), .b(sprite1[4:0]), .out(subtractor_1_out));  // open: bin, bout
  Subtractor #(.width(5)) subtractor_2 (.a(out_7), .b(sprite2[4:0]), .out(subtractor_2_out));  // open: bin, bout
  Subtractor #(.width(5)) subtractor_3 (.a(out_7), .b(sprite3[4:0]), .out(subtractor_3_out));  // open: bin, bout
  Comparator #(.width(5)) comparator_1 (.a(subtractor_1_out), .b(5'b00011), .lt(comparator_1_lt));  // open: gt, eq
  or or_1 (or_1_out, comparator_2_gt, comparator_2_eq);
  Comparator #(.width(5)) comparator_2 (
    .a(subtractor_1_out), .b({5{1'b0}}), .gt(comparator_2_gt), .eq(comparator_2_eq));  // open: lt
  Comparator #(.width(5)) comparator_3 (.a(subtractor_2_out), .b(5'b00011), .lt(comparator_3_lt));  // open: gt, eq
  or or_2 (or_2_out, comparator_4_gt, comparator_4_eq);
  Comparator #(.width(5)) comparator_4 (
    .a(subtractor_2_out), .b({5{1'b0}}), .gt(comparator_4_gt), .eq(comparator_4_eq));  // open: lt
  Comparator #(.width(5)) comparator_5 (.a(subtractor_3_out), .b(5'b00011), .lt(comparator_5_lt));  // open: gt, eq
  or or_3 (or_3_out, comparator_6_gt, comparator_6_eq);
  Comparator #(.width(5)) comparator_6 (
    .a(subtractor_3_out), .b({5{1'b0}}), .gt(comparator_6_gt), .eq(comparator_6_eq));  // open: lt
  and and_1 (and_1_out, comparator_1_lt, sprite1[5], or_1_out);
  and and_2 (and_2_out, comparator_5_lt, sprite3[5], or_3_out);
  super_mux super_mux_1 (.in_1(and_1_out), .in_2(subtractor_1_out[1:0]), .out_3(super_mux_1_out_3));
  and and_3 (and_3_out, comparator_3_lt, sprite2[5], or_2_out);
  super_mux3 super_mux3_1 (.in_1(and_2_out), .in_2(subtractor_3_out[1:0]), .out_3(super_mux3_1_out_3));
  super_mux2 super_mux2_1 (.in_1(and_3_out), .in_2(subtractor_2_out[1:0]), .out_3(super_mux2_1_out_3));
  Register #(.width(16)) register_1 (.D(in_5), .Q(out_12), .clk(in_6));  // open: en, clr
  Shifter #(.width(32), .shift("lr")) shifter_1 (.in(super_mux_1_out_3), .\dist (sprite1[10:6]), .out(shifter_1_out));
  Shifter #(.width(32), .shift("lr")) shifter_2 (.in(super_mux2_1_out_3), .\dist (sprite2[10:6]), .out(shifter_2_out));
  Shifter #(.width(32), .shift("lr")) shifter_3 (.in(super_mux3_1_out_3), .\dist (sprite3[10:6]), .out(shifter_3_out));
  // Probe on shifter_1_out
  // Probe on shifter_2_out
  // Probe on shifter_3_out
  assign out_9 = shifter_1_out | shifter_2_out | shifter_3_out | {{14{1'b0}}, out_12, 2'b11};  // OR_Gate or_4, 32 bits wide

  assign out_13 = in_6;
  assign sprite1_2 = sprite1;
  assign sprite2_2 = sprite2;
  assign sprite3_2 = sprite3;
  // also tied to GND on the sheet: {shifter_3_out[0], shifter_3_out[1], shifter_3_out[2], shifter_3_out[3], shifter_3_out[4], shifter_3_out[5], shifter_3_out[6], shifter_3_out[7], shifter_3_out[8], shifter_3_out[9], shifter_3_out[10], shifter_3_out[11], shifter_3_out[12], shifter_3_out[13], shifter_3_out[14], shifter_3_out[15], shifter_3_out[16], shifter_3_out[17], shifter_3_out[18], shifter_3_out[19], shifter_3_out[20], shifter_3_out[21], shifter_3_out[22], shifter_3_out[23], shifter_3_out[24], shifter_3_out[25], shifter_3_out[26], shifter_3_out[27], shifter_3_out[28], shifter_3_out[29], shifter_3_out[30], shifter_3_out[31], shifter_2_out[0], shifter_2_out[1], shifter_2_out[2], shifter_2_out[3], shifter_2_out[4], shifter_2_out[5], shifter_2_out[6], shifter_2_out[7], shifter_2_out[8], shifter_2_out[9], shifter_2_out[10], shifter_2_out[11], shifter_2_out[12], shifter_2_out[13], shifter_2_out[14], shifter_2_out[15], shifter_2_out[16], shifter_2_out[17], shifter_2_out[18], shifter_2_out[19], shifter_2_out[20], shifter_2_out[21], shifter_2_out[22], shifter_2_out[23], shifter_2_out[24], shifter_2_out[25], shifter_2_out[26], shifter_2_out[27], shifter_2_out[28], shifter_2_out[29], shifter_2_out[30], shifter_2_out[31]}
endmodule

module sprite1 (
  input  [1:0] in_1,
  output [31:0] out_2
);

  Multiplexer #(.select(2), .width(3), .enable("false")) multiplexer_1 (
    .in0(3'b001), .in1(3'b110), .in2(3'b101), .out(out_2[31:29]), .sel(in_1));  // open: in3

  assign out_2[28:0] = {29{1'b0}};
endmodule

module sprite2 (
  input  [1:0] in_1,
  output [31:0] out_2
);

  Multiplexer #(.select(2), .width(3), .enable("false")) multiplexer_1 (
    .in0(3'b111), .in1(3'b010), .in2(3'b011), .out(out_2[31:29]), .sel(in_1));  // open: in3

  assign out_2[28:0] = {29{1'b0}};
endmodule

module sprite3 (
  input  [1:0] in_1,
  output [31:0] out_2
);

  Multiplexer #(.select(2), .width(3), .enable("false")) multiplexer_1 (
    .in0(3'b100), .in1(3'b111), .in2(3'b110), .out(out_2[31:29]), .sel(in_1));  // open: in3

  assign out_2[28:0] = {29{1'b0}};
endmodule

module super_mux (
  input  in_1,
  input  [1:0] in_2,
  output [31:0] out_3
);

  wire [31:0] sprite1_1_out_2;

  sprite1 sprite1_1 (.out_2(sprite1_1_out_2), .in_1(in_2));
  Multiplexer #(.width(32), .enable("false")) multiplexer_1 (
    .in0({32{1'b0}}), .in1(sprite1_1_out_2), .out(out_3), .sel(in_1));
endmodule

module super_mux2 (
  input  in_1,
  input  [1:0] in_2,
  output [31:0] out_3
);

  wire [31:0] sprite2_1_out_2;

  sprite2 sprite2_1 (.out_2(sprite2_1_out_2), .in_1(in_2));
  Multiplexer #(.width(32), .enable("false")) multiplexer_1 (
    .in0({32{1'b0}}), .in1(sprite2_1_out_2), .out(out_3), .sel(in_1));
endmodule

module super_mux3 (
  input  in_1,
  input  [1:0] in_2,
  output [31:0] out_3
);

  wire [31:0] sprite3_1_out_2;

  sprite3 sprite3_1 (.out_2(sprite3_1_out_2), .in_1(in_2));
  Multiplexer #(.width(32), .enable("false")) multiplexer_1 (
    .in0({32{1'b0}}), .in1(sprite3_1_out_2), .out(out_3), .sel(in_1));
endmodule
